# Fritzing sketch shiftRegLay (saved by Fritzing 0.9.3b)
breadboards: 1

parts:
  Part1 = Arduino Uno (Rev3)
  U1 = PCF8574 [package="DIP16 [THT]"]
  LED1 = smd LED [color="Green (555nm)" package="0805 [SMD]"]
  LED2 = smd LED [color="Green (555nm)" package="0805 [SMD]"]
  LED3 = smd LED [color="Green (555nm)" package="0805 [SMD]"]
  R1 = Resistor [tolerance=±5% resistance=560 package="0402 [SMD]"]
  R2 = Resistor [tolerance=±5% resistance=560 package="0402 [SMD]"]
  R3 = Resistor [tolerance=±5% resistance=560 package="0402 [SMD]"]
  R4 = Resistor [tolerance=±5% resistance=560 package="0402 [SMD]"]
  R5 = Resistor [tolerance=±5% resistance=560 package="0402 [SMD]"]
  R6 = Resistor [tolerance=±5% resistance=560 package="0402 [SMD]"]
  R7 = Resistor [tolerance=±5% resistance=560 package="0402 [SMD]"]
  R8 = Resistor [tolerance=±5% resistance=560 package="0402 [SMD]"]
  LED4 = smd LED [color="White (8000K)" package="0805 [SMD]"]
  LED5 = smd LED [color="Red (633nm)" package="0805 [SMD]"]
  LED6 = smd LED [color="Red (633nm)" package="0805 [SMD]"]
  LED7 = smd LED [color="Red (633nm)" package="0805 [SMD]"]
  LED8 = smd LED [color="White (8000K)" package="0805 [SMD]"]
  J1 = Piezo Speaker
  R9 = Rotary Potentiometer (Small) [maximum_resistance=100kΩ package=THT]
  S1 = Momentary Switch [package=ksa_sealed_tac_switch]
  S2 = Momentary Switch [package=ksa_sealed_tac_switch]
  R10 = Resistor [tolerance=±5% resistance=10k package="0402 [SMD]"]
  R11 = Resistor [tolerance=±5% resistance=10k package="0402 [SMD]"]

nets:
  N1: Part1.D8, U1.P6
  N2: Part1.D9_PWM, U1.P7
  N3: Part1.D10_PWM/SS, U1.SCL
  N4: Part1.D13/SCK, J1.pin2
  N5: Part1.D2, S1.4, R10.Pin_0
  N6: Part1.D3_PWM, S2.4, R11.Pin_0
  5V: Part1.5V, U1.P5, U1.VCC, R9.leg2, R10.Pin_1, R11.Pin_1
  GND: Part1.GND, U1.GND, U1.INT, R1.Pin_1, R2.Pin_1, R3.Pin_0, R4.Pin_0, R5.Pin_0, R6.Pin_0, R7.Pin_1, R8.Pin_1, J1.pin1, R9.leg1, S1.2, S2.2
  N7: U1.A0, LED3.cathode
  N8: U1.A1, LED2.cathode
  N9: U1.A2, LED4.cathode
  N10: U1.P0, LED5.cathode
  N11: U1.P1, LED7.cathode
  N12: U1.P2, LED6.cathode
  N13: U1.P3, LED8.cathode
  N14: U1.SDA, LED1.cathode
  N15: LED1.anode, R1.Pin_0
  N16: LED2.anode, R7.Pin_0
  N17: LED3.anode, R8.Pin_0
  N18: R2.Pin_0, LED4.anode
  N19: R3.Pin_1, LED8.anode
  N20: R4.Pin_1, LED6.anode
  N21: R5.Pin_1, LED7.anode
  N22: R6.Pin_1, LED5.anode
